// Logisim project EE203_PROJECT.circ as structural Verilog: 7 circuits, main circuit main
module main (
  output Cout,
  output Overflow,
  output Done
);

  wire clock_1_out, control_logic_1_asen, control_logic_1_bin, control_logic_1_bout, control_logic_1_clear,
       control_logic_1_dinout, control_logic_1_irin, control_logic_1_rxout_ain, counter_2_carry,
       decimal_1_sign, decimal_2_sign, decimal_3_sign, decimal_4_sign, decimal_5_sign, decimal_6_sign,
       decimal_7_sign, decimal_8_sign, or_1_out;
  wire [1:0] counter_2_q;
  wire [2:0] control_logic_1_r0out___r7out;
  wire [3:0] decimal_1_lsb, decimal_1_mid, decimal_1_ms, decimal_2_lsb, decimal_2_mid, decimal_2_ms,
       decimal_3_lsb, decimal_3_mid, decimal_3_ms, decimal_4_lsb, decimal_4_mid, decimal_4_ms, decimal_5_lsb,
       decimal_5_mid, decimal_5_ms, decimal_6_lsb, decimal_6_mid, decimal_6_ms, decimal_7_lsb, decimal_7_mid,
       decimal_7_ms, decimal_8_lsb, decimal_8_mid, decimal_8_ms;
  wire [4:0] counter_1_q;
  wire [7:0] _0, _1, _2, _3, _4, _5, _6, _7, A_q, B_q, combined_muxs_1_output, control_logic_1_r0in, IR_q,
       n8_bit_alu_1_output, rom_1_data;

  _7_Segment_Display u_7_segment_display_1 (.g(decimal_1_sign));  // open: f, a, b, e, d, c, dp
  decimal decimal_1 (.in_1(_0), .sign(decimal_1_sign), .ms(decimal_1_ms), .mid(decimal_1_mid), .lsb(decimal_1_lsb));
  _7_Segment_Display u_7_segment_display_2 (.g(decimal_2_sign));  // open: f, a, b, e, d, c, dp
  decimal decimal_2 (.in_1(_2), .sign(decimal_2_sign), .ms(decimal_2_ms), .mid(decimal_2_mid), .lsb(decimal_2_lsb));
  _7_Segment_Display u_7_segment_display_3 (.g(decimal_3_sign));  // open: f, a, b, e, d, c, dp
  decimal decimal_3 (.in_1(_4), .sign(decimal_3_sign), .ms(decimal_3_ms), .mid(decimal_3_mid), .lsb(decimal_3_lsb));
  _7_Segment_Display u_7_segment_display_4 (.g(decimal_4_sign));  // open: f, a, b, e, d, c, dp
  decimal decimal_4 (.in_1(_6), .sign(decimal_4_sign), .ms(decimal_4_ms), .mid(decimal_4_mid), .lsb(decimal_4_lsb));
  // Probe on _0
  Hex_Digit_Display hex_digit_display_1 (.value(decimal_1_mid));  // open: dp
  Hex_Digit_Display hex_digit_display_2 (.value(decimal_1_ms));  // open: dp
  // Probe on _2
  Hex_Digit_Display hex_digit_display_3 (.value(decimal_2_ms));  // open: dp
  Hex_Digit_Display hex_digit_display_4 (.value(decimal_2_mid));  // open: dp
  // Probe on _4
  Hex_Digit_Display hex_digit_display_5 (.value(decimal_3_mid));  // open: dp
  Hex_Digit_Display hex_digit_display_6 (.value(decimal_3_ms));  // open: dp
  // Probe on _6
  Hex_Digit_Display hex_digit_display_7 (.value(decimal_4_mid));  // open: dp
  Hex_Digit_Display hex_digit_display_8 (.value(decimal_4_ms));  // open: dp
  Hex_Digit_Display hex_digit_display_9 (.value(decimal_1_lsb));  // open: dp
  Hex_Digit_Display hex_digit_display_10 (.value(decimal_2_lsb));  // open: dp
  Hex_Digit_Display hex_digit_display_11 (.value(decimal_3_lsb));  // open: dp
  Hex_Digit_Display hex_digit_display_12 (.value(decimal_4_lsb));  // open: dp
  decimal decimal_5 (.in_1(_1), .sign(decimal_5_sign), .ms(decimal_5_ms), .mid(decimal_5_mid), .lsb(decimal_5_lsb));
  decimal decimal_6 (.in_1(_3), .sign(decimal_6_sign), .ms(decimal_6_ms), .mid(decimal_6_mid), .lsb(decimal_6_lsb));
  decimal decimal_7 (.in_1(_5), .sign(decimal_7_sign), .ms(decimal_7_ms), .mid(decimal_7_mid), .lsb(decimal_7_lsb));
  decimal decimal_8 (.in_1(_7), .sign(decimal_8_sign), .ms(decimal_8_ms), .mid(decimal_8_mid), .lsb(decimal_8_lsb));
  // Probe on _1
  _7_Segment_Display u_7_segment_display_5 (.g(decimal_5_sign));  // open: f, a, b, e, d, c, dp
  Hex_Digit_Display hex_digit_display_13 (.value(decimal_5_ms));  // open: dp
  // Probe on _3
  _7_Segment_Display u_7_segment_display_6 (.g(decimal_6_sign));  // open: f, a, b, e, d, c, dp
  Hex_Digit_Display hex_digit_display_14 (.value(decimal_6_ms));  // open: dp
  // Probe on _5
  _7_Segment_Display u_7_segment_display_7 (.g(decimal_7_sign));  // open: f, a, b, e, d, c, dp
  Hex_Digit_Display hex_digit_display_15 (.value(decimal_7_ms));  // open: dp
  // Probe on _7
  _7_Segment_Display u_7_segment_display_8 (.g(decimal_8_sign));  // open: f, a, b, e, d, c, dp
  Hex_Digit_Display hex_digit_display_16 (.value(decimal_8_ms));  // open: dp
  Hex_Digit_Display hex_digit_display_17 (.value(decimal_5_mid));  // open: dp
  Hex_Digit_Display hex_digit_display_18 (.value(decimal_5_lsb));  // open: dp
  Hex_Digit_Display hex_digit_display_19 (.value(decimal_6_lsb));  // open: dp
  Hex_Digit_Display hex_digit_display_20 (.value(decimal_6_mid));  // open: dp
  Hex_Digit_Display hex_digit_display_21 (.value(decimal_7_lsb));  // open: dp
  Hex_Digit_Display hex_digit_display_22 (.value(decimal_7_mid));  // open: dp
  Hex_Digit_Display hex_digit_display_23 (.value(decimal_8_lsb));  // open: dp
  Hex_Digit_Display hex_digit_display_24 (.value(decimal_8_mid));  // open: dp
  Counter #(.width(5), .max('h1f)) counter_1 (.Q(counter_1_q), .clk(or_1_out));  // open: load, D, count, carry, clr
  // Probe on rom_1_data
  ROM #(.addrWidth(5)) rom_1 (.addr(counter_1_q), .data(rom_1_data));  // open: sel
  or or_1 (or_1_out, control_logic_1_dinout, counter_2_carry, control_logic_1_clear);
  Clock clock_1 (.out(clock_1_out));
  Register #(.trigger("low")) IR (.D(rom_1_data), .en(control_logic_1_irin), .Q(IR_q), .clk(clock_1_out));  // open: clr
  Counter #(.width(2), .max('h3)) counter_2 (
    .Q(counter_2_q), .carry(counter_2_carry), .clk(clock_1_out), .clr(control_logic_1_clear));  // open: load, D, count
  Register R0 (.D(combined_muxs_1_output), .en(control_logic_1_r0in[0]), .Q(_0), .clk(clock_1_out));  // open: clr
  Register R4 (.D(combined_muxs_1_output), .en(control_logic_1_r0in[4]), .Q(_4), .clk(clock_1_out));  // open: clr
  // Probe on control_logic_1_clear
  Register R1 (.D(combined_muxs_1_output), .en(control_logic_1_r0in[1]), .Q(_1), .clk(clock_1_out));  // open: clr
  Register R5 (.D(combined_muxs_1_output), .en(control_logic_1_r0in[5]), .Q(_5), .clk(clock_1_out));  // open: clr
  combined_MUXs combined_muxs_1 (
    .R0(_0), .R1(_1), .R2(_2), .R3(_3), .R4(_4), .R5(_5), .R6(_6), .R7(_7), .B(B_q), .DIN(rom_1_data),
    .OUTPUT(combined_muxs_1_output), .Bout(control_logic_1_bout), .DINout(control_logic_1_dinout),
    .R0out___R7out(control_logic_1_r0out___r7out));
  Register R2 (.D(combined_muxs_1_output), .en(control_logic_1_r0in[2]), .Q(_2), .clk(clock_1_out));  // open: clr
  Register R6 (.D(combined_muxs_1_output), .en(control_logic_1_r0in[6]), .Q(_6), .clk(clock_1_out));  // open: clr
  Control_Logic control_logic_1 (
    .IR(IR_q), .R0out___R7out(control_logic_1_r0out___r7out), .R0in(control_logic_1_r0in[0]),
    .R1in(control_logic_1_r0in[1]), .R2in(control_logic_1_r0in[2]), .R3in(control_logic_1_r0in[3]),
    .R4in(control_logic_1_r0in[4]), .R5in(control_logic_1_r0in[5]), .R6in(control_logic_1_r0in[6]),
    .R7in(control_logic_1_r0in[7]), .MS(counter_2_q[1]), .LS(counter_2_q[0]), .Done_Rxin(Done),
    .Rxout_Ain(control_logic_1_rxout_ain), .Asen(control_logic_1_asen), .Bin(control_logic_1_bin),
    .DINout(control_logic_1_dinout), .Bout(control_logic_1_bout), .IRin(control_logic_1_irin),
    .Clear(control_logic_1_clear));  // open: Run, Reset, Ryout
  Register R3 (.D(combined_muxs_1_output), .en(control_logic_1_r0in[3]), .Q(_3), .clk(clock_1_out));  // open: clr
  Register R7 (.D(combined_muxs_1_output), .en(control_logic_1_r0in[7]), .Q(_7), .clk(clock_1_out));  // open: clr
  Register A (.D(combined_muxs_1_output), .en(control_logic_1_rxout_ain), .Q(A_q), .clk(clock_1_out));  // open: clr
  // Probe on combined_muxs_1_output
  _8_bit_ALU u_8_bit_alu_1 (
    .B(combined_muxs_1_output), .A(A_q), .Overflow(Overflow), .OUTPUT(n8_bit_alu_1_output), .Cout(Cout),
    .Asen(control_logic_1_asen));
  // Probe on n8_bit_alu_1_output
  Register B (.D(n8_bit_alu_1_output), .en(control_logic_1_bin), .Q(B_q), .clk(clock_1_out));  // open: clr
  // Probe on B_q

  // Notes on the sheet:
  //   R0
  //   R2
  //   R4
  //   R6
  //   R7
  //   R1
  //   R3
  //   R5
  //   Q3.1
  //   2) 35
  //   4) B5
  //   5) AD
  //   6) EE
  //   1) 68 B8
  //   3) 68 6F
  //   contents of rom_1 (hex, n*v repeats v):
  //   68 b8 35 68 6f b5 ad ee 4*0 40 1 48 1f 10 c1 c2 c2
  //   DINout
  //   Q3.3
  //   1) 40 01
  //   2) 48 1F
  //   3) 10
  //   4) C1
  //   5) C2
  //   6) C2
  //   clear
  //   gives 1 when the counter reaches the max value.
endmodule

module _8_bit_ALU (
  input  [7:0] B,
  input  [7:0] A,
  input  Asen,
  output Overflow,
  output Cout,
  output [7:0] OUTPUT
);

  wire n1_bit_alu_2_ci_1, n1_bit_alu_3_ci_1, n1_bit_alu_4_ci_1, n1_bit_alu_5_ci_1, n1_bit_alu_6_ci_1,
       n1_bit_alu_7_ci_1, n1_bit_alu_8_ci_1, not_1_out;

  not not_1 (not_1_out, Asen);
  xor xor_1 (Overflow, Cout, n1_bit_alu_2_ci_1);
  _1_bit_ALU u_1_bit_alu_1 (
    .S0(not_1_out), .Ci(n1_bit_alu_2_ci_1), .S1(Asen), .Ai(A[7]), .Fi(OUTPUT[7]), .Ci_1(Cout), .Bi(B[7]));  // open: Xi, Yi
  _1_bit_ALU u_1_bit_alu_2 (
    .S0(not_1_out), .Ci(n1_bit_alu_3_ci_1), .S1(Asen), .Ai(A[6]), .Fi(OUTPUT[6]), .Ci_1(n1_bit_alu_2_ci_1),
    .Bi(B[6]));  // open: Xi, Yi
  _1_bit_ALU u_1_bit_alu_3 (
    .S0(not_1_out), .Ci(n1_bit_alu_4_ci_1), .S1(Asen), .Ai(A[5]), .Fi(OUTPUT[5]), .Ci_1(n1_bit_alu_3_ci_1),
    .Bi(B[5]));  // open: Xi, Yi
  _1_bit_ALU u_1_bit_alu_4 (
    .S0(not_1_out), .Ci(n1_bit_alu_5_ci_1), .S1(Asen), .Ai(A[4]), .Fi(OUTPUT[4]), .Ci_1(n1_bit_alu_4_ci_1),
    .Bi(B[4]));  // open: Xi, Yi
  _1_bit_ALU u_1_bit_alu_5 (
    .S0(not_1_out), .Ci(n1_bit_alu_6_ci_1), .S1(Asen), .Ai(A[3]), .Fi(OUTPUT[3]), .Ci_1(n1_bit_alu_5_ci_1),
    .Bi(B[3]));  // open: Xi, Yi
  _1_bit_ALU u_1_bit_alu_6 (
    .S0(not_1_out), .Ci(n1_bit_alu_7_ci_1), .S1(Asen), .Ai(A[2]), .Fi(OUTPUT[2]), .Ci_1(n1_bit_alu_6_ci_1),
    .Bi(B[2]));  // open: Xi, Yi
  _1_bit_ALU u_1_bit_alu_7 (
    .S0(not_1_out), .Ci(n1_bit_alu_8_ci_1), .S1(Asen), .Ai(A[1]), .Fi(OUTPUT[1]), .Ci_1(n1_bit_alu_7_ci_1),
    .Bi(B[1]));  // open: Xi, Yi
  _1_bit_ALU u_1_bit_alu_8 (
    .S0(not_1_out), .Ci(Asen), .S1(Asen), .Ai(A[0]), .Fi(OUTPUT[0]), .Ci_1(n1_bit_alu_8_ci_1), .Bi(B[0]));  // open: Xi, Yi

  // Notes on the sheet:
  //   s0
  //   s1
endmodule

module _1_bit_ALU (
  input  S0,
  input  Ci,
  input  S1,
  input  Ai,
  input  Bi,
  output Xi,
  output Fi,
  output Ci_1,
  output Yi
);

  wire and_1_out, and_2_out, and_3_out, and_4_out, not_1_out, not_2_out;

  and and_1 (and_1_out, S0, S1);
  not not_1 (not_1_out, S0);
  xor xor_1 (Xi, and_1_out, Ai);
  and and_2 (and_2_out, S1, not_1_out);
  not not_2 (not_2_out, Bi);
  and and_3 (and_3_out, S0, Bi);
  or or_1 (Yi, and_3_out, and_4_out);
  and and_4 (and_4_out, and_2_out, not_2_out);
  Adder #(.width(1)) adder_1 (.a(Xi), .b(Yi), .out(Fi), .cin(Ci), .cout(Ci_1));
endmodule

module Control_Logic (
  input  Run,
  input  Reset,
  input  [7:0] IR,
  input  MS,
  input  LS,
  output [2:0] R0out___R7out,
  output R0in,
  output R1in,
  output R2in,
  output R3in,
  output R4in,
  output R5in,
  output R6in,
  output Done_Rxin,
  output Rxout_Ain,
  output R7in,
  output Ryout,
  output Bin,
  output Bout,
  output Asen,
  output DINout,
  output IRin,
  output Clear
);

  control control_1 (
    .OP0(IR[7]), .Done_Rxin_(Done_Rxin), .OP1(IR[6]), .MS(MS), .Rxout_Ain(Rxout_Ain), .LS(LS), .Ryout(Ryout),
    .Bin(Bin), .Bout(Bout), .Asen(Asen), .DINout(DINout), .IRin(IRin), .Clear(Clear));
  Multiplexer #(.width(3), .disabled(0), .enable("false")) multiplexer_1 (
    .in0(IR[2:0]), .in1(IR[5:3]), .out(R0out___R7out), .sel(Rxout_Ain));
  Decoder #(.select(3), .disabled(0)) decoder_1 (
    .out0(R0in), .out1(R1in), .out2(R2in), .out3(R3in), .out4(R4in), .out5(R5in), .out6(R6in), .out7(R7in),
    .sel(IR[5:3]), .en(Done_Rxin));

  // Notes on the sheet:
  //   op0
  //   op1
endmodule

module combined_MUXs (
  input  [7:0] R0,
  input  [7:0] R1,
  input  [7:0] R2,
  input  [7:0] R3,
  input  [7:0] R4,
  input  [7:0] R5,
  input  [7:0] R6,
  input  [7:0] R7,
  input  [7:0] B,
  input  Bout,
  input  DINout,
  input  [7:0] DIN,
  input  [2:0] R0out___R7out,
  output [7:0] OUTPUT
);

  wire [7:0] multiplexer_1_out, multiplexer_2_out;

  // Probe on multiplexer_1_out
  Multiplexer #(.select(3), .width(8), .enable("false")) multiplexer_1 (
    .in0(R0), .in1(R1), .in2(R2), .in3(R3), .in4(R4), .in5(R5), .in6(R6), .in7(R7), .out(multiplexer_1_out),
    .sel(R0out___R7out));
  Multiplexer #(.width(8), .enable("false")) multiplexer_2 (
    .in0(multiplexer_1_out), .in1(B), .out(multiplexer_2_out), .sel(Bout));
  Multiplexer #(.width(8), .enable("false")) multiplexer_3 (
    .in0(multiplexer_2_out), .in1(DIN), .out(OUTPUT), .sel(DINout));
endmodule

module control (
  input  OP0,
  input  OP1,
  input  MS,
  input  LS,
  output Done_Rxin_,
  output Rxout_Ain,
  output Ryout,
  output Bin,
  output Bout,
  output Asen,
  output DINout,
  output IRin,
  output Clear
);

  wire and_1_out, and_2_out, and_8_out, and_9_out, not_1_out, not_2_out, not_3_out, not_4_out, not_5_out,
       not_6_out, not_7_out, not_8_out, not_9_out, not_10_out, not_11_out, not_12_out, not_13_out,
       not_14_out, not_15_out;

  not not_1 (not_1_out, OP0);
  and and_1 (and_1_out, not_1_out, not_2_out, LS);
  not not_2 (not_2_out, MS);
  and and_2 (and_2_out, OP0, MS, LS);
  and and_3 (Rxout_Ain, OP0, not_3_out, LS);
  not not_3 (not_3_out, MS);
  not not_4 (not_4_out, OP0);
  not not_5 (not_5_out, OP1);
  not not_6 (not_6_out, MS);
  not not_7 (not_7_out, LS);
  and and_4 (Bin, OP0, MS, not_8_out);
  not not_8 (not_8_out, LS);
  and and_5 (Bout, OP0, MS, LS);
  not not_9 (not_9_out, LS);
  not not_10 (not_10_out, OP0);
  not not_11 (not_11_out, MS);
  not not_12 (not_12_out, MS);
  and and_6 (IRin, not_12_out, not_13_out);
  not not_13 (not_13_out, LS);
  not not_14 (not_14_out, OP0);
  and and_7 (Clear, not_14_out, MS, not_15_out);
  not not_15 (not_15_out, LS);
  or or_1 (Done_Rxin_, and_1_out, and_2_out);
  and and_8 (and_8_out, not_4_out, not_5_out, not_6_out, LS);
  or or_2 (Ryout, and_8_out, and_9_out);
  and and_9 (and_9_out, OP0, MS, not_7_out);
  and and_10 (Asen, OP0, OP1, MS, not_9_out);
  and and_11 (DINout, not_10_out, OP1, not_11_out, LS);
endmodule

module decimal (
  input  [7:0] in_1,
  output sign,
  output [3:0] ms,
  output [3:0] mid,
  output [3:0] lsb
);

  BitSelector bitselector_1 (.in(in_1), .out(sign), .sel(3'b111));
  ROM #(.dataWidth(4)) rom_1 (.addr(in_1), .data(ms));  // open: sel
  ROM #(.dataWidth(4)) rom_2 (.addr(in_1), .data(mid));  // open: sel
  ROM #(.dataWidth(4)) rom_3 (.addr(in_1), .data(lsb));  // open: sel

  // Notes on the sheet:
  //   contents of rom_1 (hex, n*v repeats v):
  //   100*0 57*1
  //   contents of rom_2 (hex, n*v repeats v):
  //   10*0 10*1 10*2 10*3 10*4 10*5 10*6 10*7 10*8 10*9 10*0 10*1 17*2 10*1 10*0 10*9 10*8 10*7 10*6 10*5
  //   10*4 10*3 10*2 10*1
  //   contents of rom_3 (hex, n*v repeats v):
  //   0 1 2 3 4 5 6 7 8 9 0 1 2 3 4 5 6 7 8 9 0 1 2 3 4 5 6 7 8 9 0 1 2 3 4 5 6 7 8 9 0 1 2 3 4 5 6 7 8 9
  //   0 1 2 3 4 5 6 7 8 9 0 1 2 3 4 5 6 7 8 9 0 1 2 3 4 5 6 7 8 9 0 1 2 3 4 5 6 7 8 9 0 1 2 3 4 5 6 7 8 9
  //   0 1 2 3 4 5 6 7 8 9 0 1 2 3 4 5 6 7 8 9 0 1 2 3 4 5 6 7 8 7 6 5 4 3 2 1 0 9 8 7 6 5 4 3 2 1 0 9 8 7
  //   6 5 4 3 2 1 0 9 8 7 6 5 4 3 2 1 0 9 8 7 6 5 4 3 2 1 0 9 8 7 6 5 4 3 2 1 0 9 8 7 6 5 4 3 2 1 0 9 8 7
  //   6 5 4 3 2 1 0 9 8 7 6 5 4 3 2 1 0 9 8 7 6 5 4 3 2 1 0 9 8 7 6 5 4 3 2 1 0 9 8 7 6 5 4 3 2 1 0 9 8 7
  //   6 5 4 3 2 1
endmodule
