// Logisim project 1-bit-alu-slice (1).circ as structural Verilog: 2 circuits, main circuit main
module main (
  input  Ai,
  input  S1,
  input  Cin,
  input  S0,
  input  Bi,
  output Xi,
  output out_7,
  output Cout,
  output Yi
);

  wire not_1_out, not_2_out, not_3_out, not_4_out, or_1_out, S0Bi_out, S1_prime_S0_prime__Ai_out,
       S1_prime_S0_prime_out, S1S0_prime_Bi_prime_out, S1S0_prime_out;

  not not_1 (not_1_out, S1);
  not not_2 (not_2_out, S0);
  or S1_prime_S0_prime (S1_prime_S0_prime_out, not_1_out, not_2_out);
  and S0Bi (S0Bi_out, S0, Bi);
  not not_3 (not_3_out, Bi);
  and S1S0_prime (S1S0_prime_out, S1, not_2_out);
  and S1_prime_S0_prime__Ai (S1_prime_S0_prime__Ai_out, Ai, S1_prime_S0_prime_out);
  and S1S0_prime_Bi_prime (S1S0_prime_Bi_prime_out, not_3_out, S1S0_prime_out);
  or or_1 (or_1_out, Ai, S1_prime_S0_prime_out);
  not not_4 (not_4_out, or_1_out);
  or or_2 (Xi, not_4_out, S1_prime_S0_prime__Ai_out);
  or or_3 (Yi, S0Bi_out, S1S0_prime_Bi_prime_out);
  Adder #(.width(1)) adder_1 (.a(Xi), .b(Yi), .out(out_7), .cin(Cin), .cout(Cout));

  // Notes on the sheet:
  //   S1S0Ai'
endmodule

module _4_bit_alu (
  input  [3:0] B,
  input  [3:0] A,
  input  S1,
  input  S0,
  input  Cin,
  output Over_Under,
  output C4,
  output [3:0] Output
);

  wire main_2_cout, main_3_cout, main_4_cout;

  xor xor_1 (Over_Under, C4, main_2_cout);
  main main_1 (
    .Ai(A[3]), .S1(S1), .S0(S0), .Bi(B[3]), .out_7(Output[3]), .Cout(C4), .Cin(main_2_cout));  // open: Xi, Yi
  main main_2 (
    .Ai(A[2]), .S1(S1), .S0(S0), .Bi(B[2]), .out_7(Output[2]), .Cout(main_2_cout), .Cin(main_3_cout));  // open: Xi, Yi
  main main_3 (
    .Ai(A[1]), .S1(S1), .S0(S0), .Bi(B[1]), .out_7(Output[1]), .Cout(main_3_cout), .Cin(main_4_cout));  // open: Xi, Yi
  main main_4 (
    .Ai(A[0]), .S1(S1), .S0(S0), .Bi(B[0]), .out_7(Output[0]), .Cout(main_4_cout), .Cin(Cin));  // open: Xi, Yi
endmodule
