// Logisim project ee203_final.circ as structural Verilog
module main (
  input  [7:0] in_1,
  input  [7:0] DIN,
  input  in_3,
  input  in_4,
  output [7:0] out_5
);

  wire clock_1_out, control_logic_1_ain, control_logic_1_asen, control_logic_1_bin, control_logic_1_bout,
       control_logic_1_clear, control_logic_1_dinout, control_logic_1_done, control_logic_1_irin,
       n8_bit_alu_1_cout, n8_bit_alu_1_overflow;
  wire [1:0] counter_1_q;
  wire [3:0] counter_2_q;
  wire [7:0] A_q, B_q, control_logic_1_r0in, control_logic_1_r0out___r7out, IR_q, muxs_1_output,
       n8_bit_alu_1_output, R0_q, R1_q, R2_q, R3_q, R4_q, R5_q, R6_q, R7_q;

  Clock clock_1 (.out(clock_1_out));
  Register R0 (.D(muxs_1_output), .en(control_logic_1_r0in[0]), .Q(R0_q), .clk(clock_1_out));  // open: clr
  Register R4 (.D(muxs_1_output), .en(control_logic_1_r0in[4]), .Q(R4_q), .clk(clock_1_out));  // open: clr
  Register IR (.D(DIN), .en(control_logic_1_irin), .Q(IR_q), .clk(clock_1_out));  // open: clr
  Counter #(.width(2), .max('h3)) counter_1 (
    .Q(counter_1_q), .clk(clock_1_out), .clr(control_logic_1_clear));  // open: load, D, count, carry
  Register R1 (.D(muxs_1_output), .en(control_logic_1_r0in[1]), .Q(R1_q), .clk(clock_1_out));  // open: clr
  Register R5 (.D(muxs_1_output), .en(control_logic_1_r0in[5]), .Q(R5_q), .clk(clock_1_out));  // open: clr
  Control_Logic control_logic_1 (
    .IR(IR_q), .MSB(counter_1_q[1]), .LSB(counter_1_q[0]), .R0out___R7out(control_logic_1_r0out___r7out),
    .Bout(control_logic_1_bout), .DINout(control_logic_1_dinout), .R0in(control_logic_1_r0in[0]),
    .R1in(control_logic_1_r0in[1]), .R2in(control_logic_1_r0in[2]), .R3in(control_logic_1_r0in[3]),
    .R4in(control_logic_1_r0in[4]), .R5in(control_logic_1_r0in[5]), .R6in(control_logic_1_r0in[6]),
    .R7in(control_logic_1_r0in[7]), .Ain(control_logic_1_ain), .Asen(control_logic_1_asen),
    .Bin(control_logic_1_bin), .Done(control_logic_1_done), .Clear(control_logic_1_clear),
    .IRin(control_logic_1_irin));  // open: Run, Reset
  Register R2 (.D(muxs_1_output), .en(control_logic_1_r0in[2]), .Q(R2_q), .clk(clock_1_out));  // open: clr
  Register R6 (.D(muxs_1_output), .en(control_logic_1_r0in[6]), .Q(R6_q), .clk(clock_1_out));  // open: clr
  MUXs muxs_1 (
    .B(B_q), .R0(R0_q), .R1(R1_q), .R2(R2_q), .R3(R3_q), .R4(R4_q), .R5(R5_q), .R6(R6_q), .R7(R7_q),
    .DIN(DIN), .OUTPUT(muxs_1_output), .Bout(control_logic_1_bout), .DINout(control_logic_1_dinout),
    .R0_2(control_logic_1_r0out___r7out[7]), .R1_2(control_logic_1_r0out___r7out[6]),
    .R2_2(control_logic_1_r0out___r7out[5]), .R3_2(control_logic_1_r0out___r7out[4]),
    .R4_2(control_logic_1_r0out___r7out[3]), .R5_2(control_logic_1_r0out___r7out[2]),
    .R6_2(control_logic_1_r0out___r7out[1]), .R7_2(control_logic_1_r0out___r7out[0]));
  Register R3 (.D(muxs_1_output), .en(control_logic_1_r0in[3]), .Q(R3_q), .clk(clock_1_out));  // open: clr
  Register R7 (.D(muxs_1_output), .en(control_logic_1_r0in[7]), .Q(R7_q), .clk(clock_1_out));  // open: clr
  Register A (.D(muxs_1_output), .en(control_logic_1_ain), .Q(A_q), .clk(clock_1_out));  // open: clr
  _8_bit_alu u_8_bit_alu_1 (
    .A(A_q), .B(muxs_1_output), .OUTPUT(n8_bit_alu_1_output), .Overflow(n8_bit_alu_1_overflow),
    .Cout(n8_bit_alu_1_cout), .Asen(control_logic_1_asen));
  Register B (.D(n8_bit_alu_1_output), .en(control_logic_1_bin), .Q(B_q), .clk(clock_1_out));  // open: clr
  Counter #(.width(4), .max('hf)) counter_2 (.Q(counter_2_q), .clk(in_4));  // open: load, D, count, carry, clr
  RAM #(.addrWidth(2), .bus("separate")) ram_1 (
    .addr(counter_2_q[1:0]), .din(in_1), .data(out_5), .str(in_3), .clk(in_4));  // open: sel, ld, clr
  // Pins of 2 and 4 bits meet at counter_2_q
endmodule

module _8_bit_alu (
  input  [7:0] A,
  input  [7:0] B,
  input  Asen,
  output Overflow,
  output Cout,
  output [7:0] OUTPUT
);

  wire n4_bit_alu_2_c4, not_1_out;

  _4_bit_alu u_4_bit_alu_1 (
    .C4(Cout), .Output(OUTPUT[7:4]), .Over_Under(Overflow), .B(B[7:4]), .A(A[7:4]), .Cin(n4_bit_alu_2_c4),
    .S1(Asen), .S0(not_1_out));
  _4_bit_alu u_4_bit_alu_2 (
    .C4(n4_bit_alu_2_c4), .Output(OUTPUT[3:0]), .B(B[3:0]), .A(A[3:0]), .Cin(Asen), .S1(Asen), .S0(not_1_out));  // open: Over_Under
  not not_1 (not_1_out, Asen);
endmodule

module MUXs (
  input  [7:0] B,
  input  [7:0] R0,
  input  [7:0] R1,
  input  [7:0] R2,
  input  [7:0] R3,
  input  [7:0] R4,
  input  [7:0] R5,
  input  [7:0] R6,
  input  [7:0] R7,
  input  [7:0] DIN,
  input  R0_2,
  input  R1_2,
  input  R2_2,
  input  R3_2,
  input  R4_2,
  input  R5_2,
  input  R6_2,
  input  R7_2,
  input  Bout,
  input  DINout,
  output [7:0] OUTPUT
);

  wire [2:0] priority_encoder_1_out;
  wire [7:0] multiplexer_1_out, multiplexer_2_out;

  Multiplexer #(.select(3), .width(8), .enable("false")) multiplexer_1 (
    .in0(R0), .in1(R1), .in2(R2), .in3(R3), .in4(R4), .in5(R5), .in6(R6), .in7(R7), .out(multiplexer_1_out),
    .sel(priority_encoder_1_out));
  Priority_Encoder priority_encoder_1 (
    .in0(R0_2), .in1(R1_2), .in2(R2_2), .in3(R3_2), .in4(R4_2), .in5(R5_2), .in6(R6_2), .in7(R7_2),
    .out(priority_encoder_1_out));  // open: en_in
  Multiplexer #(.width(8), .enable("false")) multiplexer_2 (
    .in0(multiplexer_1_out), .in1(B), .out(multiplexer_2_out), .sel(Bout));
  Multiplexer #(.width(8), .enable("false")) multiplexer_3 (
    .in0(multiplexer_2_out), .in1(DIN), .out(OUTPUT), .sel(DINout));
endmodule

module Control_Logic (
  input  [7:0] IR,
  input  Run,
  input  Reset,
  input  MSB,
  input  LSB,
  output [7:0] R0out___R7out,
  output Bout,
  output DINout,
  output R0in,
  output R1in,
  output R2in,
  output R3in,
  output R4in,
  output R5in,
  output R6in,
  output R7in,
  output Ain,
  output Asen,
  output Bin,
  output Done,
  output Clear,
  output IRin
);

  wire [1:0] Rxout_rxout;
  wire [2:0] multiplexer_1_out, multiplexer_2_out;

  Rxout Rxout (.OP1(IR[7]), .OP0(IR[6]), .MSB(MSB), .LSB(LSB), .Rxout(Rxout_rxout[0]));
  Ryout Ryout (.OP1(IR[7]), .OP0(IR[6]), .MSB(MSB), .LSB(LSB), .Ryout(Rxout_rxout[1]));
  Done_Rxin Done_Rxin (.MSB(MSB), .LSB(LSB), .OP1(IR[7]), .OP0(IR[6]), .Done(Done));
  Bin u_Bin (.MSB(MSB), .LSB(LSB), .OP1(IR[7]), .OP0(IR[6]), .Bin(Bin));
  Ain u_Ain (.OP1(IR[7]), .OP0(IR[6]), .MSB(MSB), .LSB(LSB), .Ain(Ain));
  DINout u_DINout (.OP1(IR[7]), .OP0(IR[6]), .MSB(MSB), .LSB(LSB), .DINout(DINout));
  Asen u_Asen (.OP1(IR[7]), .OP0(IR[6]), .MSB(MSB), .LSB(LSB), .Asen(Asen));
  Bout u_Bout (.OP1(IR[7]), .OP0(IR[6]), .MSB(MSB), .LSB(LSB), .Bout(Bout));
  IRin RIin (.OP1(IR[7]), .OP0(IR[6]), .MSB(MSB), .LSB(LSB), .RIin(IRin));
  Clear u_Clear (.OP1(IR[7]), .OP0(IR[6]), .MSB(MSB), .LSB(LSB), .Clear(Clear));
  Multiplexer #(.select(2), .width(3), .enable("false")) multiplexer_1 (
    .in0(3'b000), .in1(IR[5:3]), .in2(IR[2:0]), .in3(3'b000), .out(multiplexer_1_out), .sel(Rxout_rxout));
  Multiplexer #(.width(3), .enable("false")) multiplexer_2 (
    .in0(3'b000), .in1(IR[5:3]), .out(multiplexer_2_out), .sel(Done));
  Decoder #(.select(3), .enable("false")) decoder_1 (
    .out0(R0out___R7out[7]), .out1(R0out___R7out[6]), .out2(R0out___R7out[5]), .out3(R0out___R7out[4]),
    .out4(R0out___R7out[3]), .out5(R0out___R7out[2]), .out6(R0out___R7out[1]), .out7(R0out___R7out[0]),
    .sel(multiplexer_1_out));
  Decoder #(.select(3), .enable("false")) decoder_2 (
    .out0(R0in), .out1(R1in), .out2(R2in), .out3(R3in), .out4(R4in), .out5(R5in), .out6(R6in), .out7(R7in),
    .sel(multiplexer_2_out));

  // Notes on the sheet:
  //   Out
  //   In
endmodule

module Done_Rxin (
  input  MSB,
  input  LSB,
  input  OP1,
  input  OP0,
  output Done
);

  wire not_1_out, not_2_out, not_3_out, or_1_out, or_2_out;

  or or_1 (or_1_out, MSB, not_1_out);
  not not_1 (not_1_out, OP1);
  not not_2 (not_2_out, LSB);
  not not_3 (not_3_out, MSB);
  or or_2 (or_2_out, not_3_out, OP1);
  and and_1 (Done, or_1_out, not_2_out, or_2_out);
endmodule

module Bin (
  input  MSB,
  input  LSB,
  input  OP1,
  input  OP0,
  output Bin
);

  wire not_1_out;

  not not_1 (not_1_out, MSB);
  and and_1 (Bin, not_1_out, LSB, OP1);
endmodule

module Ain (
  input  OP1,
  input  OP0,
  input  MSB,
  input  LSB,
  output Ain
);

  wire not_1_out, not_2_out;

  not not_1 (not_1_out, MSB);
  and and_1 (Ain, OP1, not_1_out, not_2_out);
  not not_2 (not_2_out, LSB);
endmodule

module DINout (
  input  OP1,
  input  OP0,
  input  MSB,
  input  LSB,
  output DINout
);

  wire not_1_out, not_2_out, not_3_out;

  not not_1 (not_1_out, OP1);
  not not_2 (not_2_out, MSB);
  not not_3 (not_3_out, LSB);
  and and_1 (DINout, not_1_out, OP0, not_2_out, not_3_out);
endmodule

module Asen (
  input  OP1,
  input  OP0,
  input  MSB,
  input  LSB,
  output Asen
);

  wire not_1_out;

  not not_1 (not_1_out, MSB);
  and and_1 (Asen, OP1, OP0, not_1_out, LSB);
endmodule

module Bout (
  input  OP1,
  input  OP0,
  input  MSB,
  input  LSB,
  output Bout
);

  wire not_1_out;

  and and_1 (Bout, OP1, MSB, not_1_out);
  not not_1 (not_1_out, LSB);
endmodule

module Rxout (
  input  OP1,
  input  OP0,
  input  MSB,
  input  LSB,
  output Rxout
);

  wire not_1_out, not_2_out;

  and and_1 (Rxout, OP1, not_1_out, not_2_out);
  not not_1 (not_1_out, MSB);
  not not_2 (not_2_out, LSB);
endmodule

module Ryout (
  input  OP1,
  input  OP0,
  input  MSB,
  input  LSB,
  output Ryout
);

  wire and_1_out, and_2_out, not_1_out, not_2_out, not_3_out, not_4_out, not_5_out;

  not not_1 (not_1_out, OP1);
  not not_2 (not_2_out, OP0);
  not not_3 (not_3_out, MSB);
  not not_4 (not_4_out, LSB);
  not not_5 (not_5_out, MSB);
  and and_1 (and_1_out, not_1_out, not_2_out, not_3_out, not_4_out);
  or or_1 (Ryout, and_1_out, and_2_out);
  and and_2 (and_2_out, OP1, not_5_out, LSB);
endmodule

module IRin (
  input  OP1,
  input  OP0,
  input  MSB,
  input  LSB,
  output RIin
);

  wire and_1_out, and_2_out, not_1_out, not_2_out, not_3_out, not_4_out;

  not not_1 (not_1_out, MSB);
  and and_1 (and_1_out, not_1_out, not_2_out);
  not not_2 (not_2_out, LSB);
  not not_3 (not_3_out, OP1);
  and and_2 (and_2_out, not_3_out, OP0, not_4_out);
  not not_4 (not_4_out, MSB);
  or or_1 (RIin, and_1_out, and_2_out);
endmodule

module Clear (
  input  OP1,
  input  OP0,
  input  MSB,
  input  LSB,
  output Clear
);

  wire and_1_out, and_2_out, not_1_out, not_2_out;

  not not_1 (not_1_out, OP1);
  not not_2 (not_2_out, MSB);
  and and_1 (and_1_out, not_1_out, not_2_out, LSB);
  and and_2 (and_2_out, OP1, MSB, LSB);
  or or_1 (Clear, and_1_out, and_2_out);
endmodule
